// Digital circuit cpu.dig as structural Verilog
module cpu (
  input  RESET,
  input  HALT,
  input  CONTINUE,
  input  CLKEN,
  input  STEP,
  input  clk,
  output IOEN,
  output IOREN,
  output IOWEN,
  output [7:0] IODATA,
  output [14:0] IOADDR
);

  wire _4x16bit_mux_1_p6, clock_1_clkout, clock_1_ishalted, clock_1_reset_2, condition_checker_1_skip,
       nand_1_out, nand_2_out, nand_3_out, nand_4_out, nand_5_out, nand_6_out, nand_7_out, nand_8_out,
       nand_9_out, nand_10_out, nand_11_out, oprom_1_p3, oprom_1_p4, oprom_1_p7, oprom_1_p8, oprom_1_p9,
       oprom_1_p11, program_memory_1_p2, program_memory_1_p9;
  wire [1:0] program_memory_1_p5, program_memory_1_p6, program_memory_1_p7;
  wire [2:0] program_memory_1_p3, program_memory_1_p4;
  wire [4:0] _8bit_alu_1_flags;
  wire [7:0] _2x8bit_mux_1_out, _2x16bit_mux_1_p2, _4x8bit_mux_1_p4, _4x8bit_mux_1_p6, program_memory_1_p8;
  wire [7:5] _8bit_alu_1_flags_2;
  wire [15:0] _4x16bit_mux_1_p1, _4x16bit_mux_1_p3, _4x16bit_mux_1_p4, program_memory_1_p1;

  clock clock_1 (
    .RESET(RESET), .HALT(HALT), .CONTINUE(CONTINUE), .CLKHALT(oprom_1_p11), .CLKIN(clk), .STEP(STEP),
    .CLKEN(CLKEN), .ISHALTED(clock_1_ishalted), .RESET_2(clock_1_reset_2), .CLKOUT(clock_1_clkout));
  LED HALTED (.in(clock_1_ishalted));
  nand nand_1 (nand_1_out, clock_1_clkout, clock_1_clkout);
  // program_memory program_memory_1: pin names not known; wires that end beside it: program_memory_1_p1, program_memory_1_p2, program_memory_1_p3, program_memory_1_p4, program_memory_1_p5, program_memory_1_p6, program_memory_1_p7, program_memory_1_p8, program_memory_1_p9
  program_counter program_counter_1 (
    .CLK(clock_1_clkout), .W(_4x16bit_mux_1_p1), .CLR(clock_1_reset_2), .R(program_memory_1_p1));
  // _4x16bit_mux _4x16bit_mux_1: pin names not known; wires that end beside it: _4x16bit_mux_1_p1, program_memory_1_p9, _4x16bit_mux_1_p3, _4x16bit_mux_1_p4, {16{1'b0}}, _4x16bit_mux_1_p6
  condition_checker condition_checker_1 (
    .FLAGS(_8bit_alu_1_flags), .COND(program_memory_1_p3), .SKIP(condition_checker_1_skip));
  // oprom oprom_1: pin names not known; wires that end beside it: program_memory_1_p2, condition_checker_1_skip, oprom_1_p3, oprom_1_p4, IOREN, IOWEN, oprom_1_p7, oprom_1_p8, oprom_1_p9, _4x16bit_mux_1_p6, oprom_1_p11
  _16bit_incrementer _16bit_incrementer_1 (.IN(program_memory_1_p1), .OUT(_4x16bit_mux_1_p4));
  // _4x8bit_mux _4x8bit_mux_1: pin names not known; wires that end beside it: oprom_1_p9, program_memory_1_p8, IODATA, _4x8bit_mux_1_p4, _4x16bit_mux_1_p3[7:0], _4x8bit_mux_1_p6
  // _2x16bit_mux _2x16bit_mux_1: pin names not known; wires that end beside it: oprom_1_p8, {_2x16bit_mux_1_p2, _4x16bit_mux_1_p3[7:0]}, program_memory_1_p9, {IOEN, IOADDR}
  _4x8bit_register_file_async_clear _4x8bit_register_file_async_clear_1 (
    .CLK(nand_1_out), .WEN(oprom_1_p3), .WRITE(_4x8bit_mux_1_p6), .R1SEL(program_memory_1_p6),
    .WSEL(program_memory_1_p5), .R2SEL(program_memory_1_p7), .CLR(clock_1_reset_2),
    .READ1(_4x16bit_mux_1_p3[7:0]), .READ2(_4x16bit_mux_1_p3[15:8]), .READP(_2x16bit_mux_1_p2));
  nand nand_2 (nand_2_out, IOEN, IOEN);
  _2x8bit_mux _2x8bit_mux_1 (
    .SEL(oprom_1_p7), .B(_4x16bit_mux_1_p3[15:8]), .A(program_memory_1_p8), .OUT(_2x8bit_mux_1_out));
  nand nand_3 (nand_3_out, IOWEN, nand_2_out);
  nand nand_4 (nand_4_out, IOREN, nand_2_out);
  _8bit_alu _8bit_alu_1 (
    .A(_4x16bit_mux_1_p3[7:0]), .B(_2x8bit_mux_1_out), .OP(program_memory_1_p4), .CLK(nand_1_out),
    .WFLAGEN(oprom_1_p4), .CLR(clock_1_reset_2), .FLAGS({_8bit_alu_1_flags_2, _8bit_alu_1_flags}),
    .RESULT(_4x8bit_mux_1_p4));
  nand nand_5 (nand_5_out, nand_3_out, nand_3_out);
  nand nand_6 (nand_6_out, nand_4_out, nand_4_out);
  nand nand_7 (nand_7_out, nand_5_out, nand_1_out);
  nand nand_8 (nand_8_out, IOREN, IOREN);
  nand nand_9 (nand_9_out, nand_7_out, nand_7_out);
  nand nand_10 (nand_10_out, IOWEN, nand_8_out);
  nand nand_11 (nand_11_out, nand_10_out, nand_10_out);
  RAMSinglePortSel #(.AddrBits(15), .Bits(8)) ramsingleportsel_1 (
    .A(IOADDR), .CS(1'b1), .WE(nand_9_out), .OE(nand_6_out), .D(IODATA));
  assign IODATA = nand_11_out ? _4x16bit_mux_1_p3[15:8] : 8'bz;  // Driver driver_1

  // Notes on the sheet:
  //   clk: Hz: 100
endmodule
